// Logisim project ALU.circ as structural Verilog: 1 circuit, main circuit main
module main (
  input  in_1,
  input  in_2,
  input  in_3,
  input  in_4,
  input  in_5,
  input  in_6,
  input  in_7,
  input  in_8,
  input  in_9,
  input  in_10,
  input  BInvert,
  input  Add_Subtract_CMD,
  input  ALU_Operation,
  input  in_14,
  output Zero,
  output Negative,
  output Overflow,
  output Result,
  output out_19,
  output out_20,
  output out_21
);

  wire A0_out, A1_out, A2_out, A3_out, and_1_out, and_2_out, and_3_out, and_4_out, and_5_out, and_6_out,
       and_7_out, and_8_out, B0_out, B1_out, B2_out, B3_out, clock_1_out, clock_2_out, d_ff_1_q, d_ff_2_q,
       d_ff_3_q, d_ff_4_q, d_ff_5_q, d_ff_6_q, d_ff_7_q, d_ff_8_q, or_1_out, or_2_out, or_3_out, or_4_out,
       xor_1_out, xor_2_out, xor_3_out, xor_4_out, xor_5_out, xor_6_out, xor_7_out, xor_8_out;

  Clock clock_1 (.out(clock_1_out));
  D_Flip_Flop d_ff_1 (.D(in_5), .clk(clock_1_out), .Q(d_ff_1_q));  // open: Qn, preset, reset
  D_Flip_Flop d_ff_2 (.D(in_6), .clk(clock_1_out), .Q(d_ff_2_q));  // open: Qn, preset, reset
  D_Flip_Flop d_ff_3 (.D(in_7), .clk(clock_1_out), .Q(d_ff_3_q));  // open: Qn, preset, reset
  D_Flip_Flop d_ff_4 (.D(in_8), .clk(clock_1_out), .Q(d_ff_4_q));  // open: Qn, preset, reset
  buf A0 (A0_out, d_ff_4_q);  // XOR_Gate
  xor A3 (A3_out, d_ff_1_q, in_10);
  xor A1 (A1_out, d_ff_3_q, in_10);
  xor A2 (A2_out, d_ff_2_q, in_10);
  xor B0 (B0_out, d_ff_8_q, BInvert);
  xor B1 (B1_out, d_ff_7_q, BInvert);
  Clock clock_2 (.out(clock_2_out));
  D_Flip_Flop d_ff_5 (.D(in_1), .clk(clock_2_out), .Q(d_ff_5_q));  // open: Qn, preset, reset
  D_Flip_Flop d_ff_6 (.D(in_2), .clk(clock_2_out), .Q(d_ff_6_q));  // open: Qn, preset, reset
  D_Flip_Flop d_ff_7 (.D(in_3), .clk(clock_2_out), .Q(d_ff_7_q));  // open: Qn, preset, reset
  xor B3 (B3_out, d_ff_5_q, BInvert);
  D_Flip_Flop d_ff_8 (.D(in_4), .clk(clock_2_out), .Q(d_ff_8_q));  // open: Qn, preset, reset
  xor B2 (B2_out, d_ff_6_q, BInvert);
  and and_1 (and_1_out, A0_out, B0_out);
  xor xor_1 (xor_1_out, A0_out, B0_out);
  xor xor_2 (xor_2_out, B1_out, A1_out);
  and and_2 (and_2_out, B1_out, A1_out);
  xor xor_3 (xor_3_out, B2_out, A2_out);
  buf and_3 (and_3_out, B2_out);  // AND_Gate
  and and_4 (and_4_out, A3_out, B3_out);
  xor xor_4 (xor_4_out, A3_out, B3_out);
  xor xor_5 (xor_5_out, in_9, xor_1_out);
  xor xor_6 (xor_6_out, or_1_out, xor_2_out);
  xor xor_7 (xor_7_out, or_2_out, xor_3_out);
  and and_5 (and_5_out, in_9, xor_1_out);
  and and_6 (and_6_out, or_1_out, xor_2_out);
  and and_7 (and_7_out, or_2_out, xor_3_out);
  xor xor_8 (xor_8_out, or_3_out, xor_4_out);
  and and_8 (and_8_out, or_3_out, xor_4_out);
  or or_1 (or_1_out, and_5_out, and_1_out);
  or or_2 (or_2_out, and_6_out, and_2_out);
  or or_3 (or_3_out, and_7_out, and_3_out);
  or or_4 (or_4_out, and_8_out, and_4_out);

  // Notes on the sheet:
  //   AInvert
  //   STUDENT NAME, STUDENT ID
  //   A
  //   A
  //   Status output
  //   sum
  //   sum
  //   carry
  //   carry
  //   carry
  //   carry
  //   R0
endmodule
