// Logisim project ALU_final.circ as structural Verilog: 13 circuits, main circuit main
module main (
  input  in_1,
  input  in_2,
  input  in_3,
  input  in_4,
  input  in_5,
  input  in_6,
  input  in_7,
  input  in_8,
  input  AInvert,
  input  BInvert,
  input  Add_Subtract_CMD,
  input  in_12,
  input  in_13,
  output Result,
  output out_15,
  output out_16,
  output out_17,
  output Sign,
  output Zero,
  output Overflow
);

  wire a_register_1_a0, a_register_1_a1, a_register_1_a2, a_register_1_a3, ALU0_carry_out, ALU0_result,
       ALU1_carry_out, ALU1_result, ALU2_carry_out, ALU2_result, ALU3_carry_out, ALU3_result,
       alu_op_register_1_s0, alu_op_register_1_s1, b_register_1_b0, b_register_1_b1, b_register_1_b2,
       b_register_1_b3, clock_1_out, d_ff_1_q, d_ff_2_q, d_ff_3_q, nor_1_out, not_1_out,
       overflow_check_1_overflow, SignBitB_c;

  Clock clock_1 (.out(clock_1_out));
  D_Flip_Flop d_ff_1 (.D(AInvert), .clk(clock_1_out), .Q(d_ff_1_q));  // open: Qn, preset, reset
  D_Flip_Flop d_ff_2 (.D(BInvert), .clk(clock_1_out), .Q(d_ff_2_q));  // open: Qn, preset, reset
  D_Flip_Flop d_ff_3 (.D(Add_Subtract_CMD), .clk(clock_1_out), .Q(d_ff_3_q));  // open: Qn, preset, reset
  ALU_OP_register alu_op_register_1 (
    .LSB(in_13), .MSB(in_12), .clk(clock_1_out), .S0(alu_op_register_1_s0), .S1(alu_op_register_1_s1));
  A_Register a_register_1 (
    .clk(clock_1_out), .A2in(in_6), .A1in(in_7), .A0in(in_8), .A3in(in_5), .A3(a_register_1_a3),
    .A2(a_register_1_a2), .A1(a_register_1_a1), .A0(a_register_1_a0));
  B_register b_register_1 (
    .clk(clock_1_out), .B2in(in_2), .B1in(in_3), .B0in(in_4), .B3in(in_1), .B3(b_register_1_b3),
    .B2(b_register_1_b2), .B1(b_register_1_b1), .B0(b_register_1_b0));
  not not_1 (not_1_out, b_register_1_b3);
  ALU ALU0 (
    .carry_in(d_ff_3_q), .A(a_register_1_a0), .MSB(alu_op_register_1_s1), .LSB(alu_op_register_1_s0),
    .A_invert(d_ff_1_q), .B(b_register_1_b0), .B_invert(d_ff_2_q), .result(ALU0_result),
    .carry_out(ALU0_carry_out));
  ALU ALU1 (
    .carry_in(ALU0_carry_out), .A(a_register_1_a1), .MSB(alu_op_register_1_s1), .LSB(alu_op_register_1_s0),
    .A_invert(d_ff_1_q), .B(b_register_1_b1), .B_invert(d_ff_2_q), .result(ALU1_result),
    .carry_out(ALU1_carry_out));
  ALU ALU2 (
    .carry_in(ALU1_carry_out), .A(a_register_1_a2), .MSB(alu_op_register_1_s1), .LSB(alu_op_register_1_s0),
    .A_invert(d_ff_1_q), .B(b_register_1_b2), .B_invert(d_ff_2_q), .result(ALU2_result),
    .carry_out(ALU2_carry_out));
  ALU ALU3 (
    .carry_in(ALU2_carry_out), .A(a_register_1_a3), .MSB(alu_op_register_1_s1), .LSB(alu_op_register_1_s0),
    .A_invert(d_ff_1_q), .B(b_register_1_b3), .B_invert(d_ff_2_q), .result(ALU3_result),
    .carry_out(ALU3_carry_out));
  multiplexer_one_bit SignBitB (.input1(b_register_1_b3), .input2(not_1_out), .S(d_ff_2_q), .C(SignBitB_c));
  nor nor_1 (nor_1_out, ALU3_result, ALU0_result, ALU1_result, ALU2_result);
  overflow_check overflow_check_1 (
    .SignBitA(a_register_1_a3), .SignBitB(SignBitB_c), .ResultSignBit(ALU3_result),
    .CarryOut(ALU3_carry_out), .AddSubCMD(d_ff_3_q), .Overflow(overflow_check_1_overflow));
  result_register result_register_1 (
    .clk(clock_1_out), .R2in(ALU2_result), .R1in(ALU1_result), .R0in(ALU0_result), .carry(ALU3_carry_out),
    .R3in(ALU3_result), .R3(Result), .R2(out_15), .R1(out_16), .R0(out_17));  // open: carryout
  status_output_register status_output_register_1 (
    .overflow(overflow_check_1_overflow), .sign(ALU3_result), .zero(nor_1_out), .clk(clock_1_out),
    .sign_bit(Sign), .zero_bit(Zero), .overflow_bit(Overflow));

  // Notes on the sheet:
  //   A
  //   ALU Operation
  //   B
  //   A0
  //   Rita Yang, 260893989
  //   overflow circuit limitations: need to be manually checked for cases like (1)-(-1) 
  //   (-1) would be seen as 15 in the unsigned overflow circuit and result in overflow
  //   Status output
endmodule

module A_Register (
  input  clk,
  input  A2in,
  input  A1in,
  input  A0in,
  input  A3in,
  output A3,
  output A2,
  output A1,
  output A0
);

  D_Flip_Flop d_ff_1 (.D(A3in), .clk(clk), .Q(A3));  // open: Qn, preset, reset
  D_Flip_Flop d_ff_2 (.D(A2in), .clk(clk), .Q(A2));  // open: Qn, preset, reset
  D_Flip_Flop d_ff_3 (.D(A1in), .clk(clk), .Q(A1));  // open: Qn, preset, reset
  D_Flip_Flop d_ff_4 (.D(A0in), .clk(clk), .Q(A0));  // open: Qn, preset, reset
endmodule

module B_register (
  input  clk,
  input  B2in,
  input  B1in,
  input  B0in,
  input  B3in,
  output B3,
  output B2,
  output B1,
  output B0
);

  D_Flip_Flop d_ff_1 (.D(B3in), .clk(clk), .Q(B3));  // open: Qn, preset, reset
  D_Flip_Flop d_ff_2 (.D(B2in), .clk(clk), .Q(B2));  // open: Qn, preset, reset
  D_Flip_Flop d_ff_3 (.D(B1in), .clk(clk), .Q(B1));  // open: Qn, preset, reset
  D_Flip_Flop d_ff_4 (.D(B0in), .clk(clk), .Q(B0));  // open: Qn, preset, reset
endmodule

module ALU_OP_register (
  input  LSB,
  input  MSB,
  input  clk,
  output S0,
  output S1
);

  D_Flip_Flop d_ff_1 (.D(LSB), .clk(clk), .Q(S0));  // open: Qn, preset, reset
  D_Flip_Flop d_ff_2 (.D(MSB), .clk(clk), .Q(S1));  // open: Qn, preset, reset
endmodule

module Add_circuit (
  input  C,
  input  A,
  input  B,
  output sum,
  output carry
);

  wire and_1_out, and_2_out, xor_1_out;

  xor xor_1 (xor_1_out, A, B);
  and and_1 (and_1_out, A, B);
  xor xor_2 (sum, C, xor_1_out);
  and and_2 (and_2_out, C, xor_1_out);
  or or_1 (carry, and_2_out, and_1_out);
endmodule

module ALU (
  input  carry_in,
  input  A,
  input  MSB,
  input  LSB,
  input  A_invert,
  input  B,
  input  B_invert,
  output result,
  output carry_out
);

  wire multiplexer_one_bit_1_c, multiplexer_one_bit_2_c, not_1_out, not_2_out, operation0_out,
       operation1_out, operation2_sum;

  not not_1 (not_1_out, A);
  not not_2 (not_2_out, B);
  multiplexer_one_bit multiplexer_one_bit_1 (.input1(A), .input2(not_1_out), .S(A_invert), .C(multiplexer_one_bit_1_c));
  multiplexer_one_bit multiplexer_one_bit_2 (.input1(B), .input2(not_2_out), .S(B_invert), .C(multiplexer_one_bit_2_c));
  and operation0 (operation0_out, multiplexer_one_bit_1_c, multiplexer_one_bit_2_c);
  or operation1 (operation1_out, multiplexer_one_bit_2_c, multiplexer_one_bit_1_c);
  Add_circuit operation2 (
    .C(carry_in), .A(multiplexer_one_bit_1_c), .B(multiplexer_one_bit_2_c), .sum(operation2_sum),
    .carry(carry_out));
  result_multiplexer result_multiplexer_1 (
    .MSB(MSB), .LSB(LSB), .input10(operation2_sum), .input01(operation1_out), .Input00(operation0_out),
    .out_result(result));
endmodule

module multiplexer_one_bit (
  input  input1,
  input  input2,
  input  S,
  output C
);

  wire and_1_out, and_2_out, not_1_out;

  not not_1 (not_1_out, S);
  and and_1 (and_1_out, input1, not_1_out);
  and and_2 (and_2_out, S, input2);
  or or_1 (C, and_1_out, and_2_out);
endmodule

module two_bit_multiplexer (
  input  operation1,
  input  operation2,
  input  S,
  output C
);

  wire and_1_out, and_2_out, not_1_out;

  not not_1 (not_1_out, S);
  and and_1 (and_1_out, operation1, not_1_out);
  and and_2 (and_2_out, S, operation2);
  or or_1 (C, and_1_out, and_2_out);
endmodule

module four_input_multiplexer (
  input  S0,
  input  S1,
  input  input11,
  input  input10,
  input  input01,
  input  Input00,
  output out_result
);

  wire and_1_out, and_2_out, and_3_out, and_4_out, not_1_out, not_2_out;

  not not_1 (not_1_out, S0);
  not not_2 (not_2_out, S1);
  and and_1 (and_1_out, S0, S1, input11);
  and and_2 (and_2_out, S0, not_2_out, input10);
  and and_3 (and_3_out, not_1_out, S1, input01);
  and and_4 (and_4_out, not_1_out, not_2_out, Input00);
  or or_1 (out_result, and_1_out, and_2_out, and_3_out, and_4_out);
endmodule

module result_multiplexer (
  input  MSB,
  input  LSB,
  input  input10,
  input  input01,
  input  Input00,
  output out_result
);

  wire and_1_out, and_2_out, and_3_out, not_1_out, not_2_out;

  not not_1 (not_1_out, MSB);
  not not_2 (not_2_out, LSB);
  and and_1 (and_1_out, MSB, not_2_out, input10);
  and and_2 (and_2_out, not_1_out, LSB, input01);
  and and_3 (and_3_out, not_1_out, not_2_out, Input00);
  or or_1 (out_result, and_1_out, and_2_out, and_3_out);
endmodule

module result_register (
  input  clk,
  input  R2in,
  input  R1in,
  input  R0in,
  input  carry,
  input  R3in,
  output R3,
  output R2,
  output R1,
  output R0,
  output carryout
);

  D_Flip_Flop d_ff_1 (.D(R3in), .clk(clk), .Q(R3));  // open: Qn, preset, reset
  D_Flip_Flop d_ff_2 (.D(R2in), .clk(clk), .Q(R2));  // open: Qn, preset, reset
  D_Flip_Flop d_ff_3 (.D(R1in), .clk(clk), .Q(R1));  // open: Qn, preset, reset
  D_Flip_Flop d_ff_4 (.D(R0in), .clk(clk), .Q(R0));  // open: Qn, preset, reset
  D_Flip_Flop d_ff_5 (.D(carry), .clk(clk), .Q(carryout));  // open: Qn, preset, reset
endmodule

module overflow_check (
  input  SignBitA,
  input  SignBitB,
  input  ResultSignBit,
  input  CarryOut,
  input  AddSubCMD,
  output Overflow
);

  wire and_1_out, not_1_out, xor_1_out, xor_2_out, xor_3_out;

  xor xor_1 (xor_1_out, SignBitA, SignBitB);
  not not_1 (not_1_out, xor_1_out);
  xor xor_2 (xor_2_out, SignBitB, ResultSignBit);
  xor xor_3 (xor_3_out, CarryOut, AddSubCMD);
  and and_1 (and_1_out, not_1_out, xor_2_out);
  or or_1 (Overflow, and_1_out, xor_3_out);

  // Notes on the sheet:
  //   Result Sign Differs from Input Sign Check
  //   UnSignedOverFlowCheck
  //   Similar Sign Check
endmodule

module status_output_register (
  input  overflow,
  input  sign,
  input  zero,
  input  clk,
  output sign_bit,
  output zero_bit,
  output overflow_bit
);

  D_Flip_Flop d_ff_1 (.D(sign), .clk(clk), .Q(sign_bit));  // open: Qn, preset, reset
  D_Flip_Flop d_ff_2 (.D(zero), .clk(clk), .Q(zero_bit));  // open: Qn, preset, reset
  D_Flip_Flop d_ff_3 (.D(overflow), .clk(clk), .Q(overflow_bit));  // open: Qn, preset, reset
endmodule
