// Logisim project KITT.circ as structural Verilog: 1 circuit, main circuit KITT
module KITT (
);

  wire clock_1_out, decoder_1_out0, decoder_1_out1, decoder_1_out2, decoder_1_out3, decoder_1_out4,
       decoder_1_out5, decoder_1_out6, decoder_1_out7, decoder_1_out8, decoder_1_out9, decoder_1_out10,
       decoder_1_out11, decoder_1_out12, decoder_1_out13, L2_out, L3_out, L4_out, L5_out, L6_out, L7_out;
  wire [3:0] counter_1_q;

  or L2 (L2_out, decoder_1_out13, decoder_1_out1);
  Decoder #(.select(4)) decoder_1 (
    .out0(decoder_1_out0), .out1(decoder_1_out1), .out2(decoder_1_out2), .out3(decoder_1_out3),
    .out4(decoder_1_out4), .out5(decoder_1_out5), .out6(decoder_1_out6), .out7(decoder_1_out7),
    .out8(decoder_1_out8), .out9(decoder_1_out9), .out10(decoder_1_out10), .out11(decoder_1_out11),
    .out12(decoder_1_out12), .out13(decoder_1_out13), .sel(counter_1_q));  // open: out14, out15, en
  Clock clock_1 (.out(clock_1_out));
  LED led_1 (.in(decoder_1_out0));
  LED led_2 (.in(L2_out));
  LED led_3 (.in(L3_out));
  LED led_4 (.in(L4_out));
  LED led_5 (.in(L5_out));
  LED led_6 (.in(L6_out));
  or L3 (L3_out, decoder_1_out12, decoder_1_out2);
  LED led_7 (.in(L7_out));
  LED led_8 (.in(decoder_1_out7));
  Counter #(.max('hd), .width(4)) counter_1 (
    .clr(1'b0), .load(1'b0), .up(1'b1), .count(1'b1), .clk(clock_1_out), .D(4'b0000), .Q(counter_1_q));  // open: carry
  or L7 (L7_out, decoder_1_out6, decoder_1_out8);
  or L6 (L6_out, decoder_1_out9, decoder_1_out5);
  or L4 (L4_out, decoder_1_out3, decoder_1_out11);
  or L5 (L5_out, decoder_1_out4, decoder_1_out10);

  // Notes on the sheet:
  //   Rita Yang, 260893989
endmodule
