// Logisim project Logism_tutorial_latches_flipflops copy.circ as structural Verilog: 1 circuit, main circuit main
module main (
  input  R,
  input  D,
  input  S,
  input  RS_Flip_flop,
  input  in_5,
  input  D_2,
  input  in_7,
  output Q,
  output Q_2,
  output nQ,
  output nQ_2,
  output Q_3,
  output out_13,
  output out_14,
  output nQ_3,
  output out_16,
  output out_17,
  output out_18
);

  wire and_1_out, and_2_out, and_3_out, and_4_out, and_5_out, and_6_out, clock_1_out, clock_2_out,
       clock_3_out, clock_4_out, clock_5_out, d_ff_2_qn, nor_5_out, nor_6_out, not_1_out, not_2_out,
       not_3_out, not_4_out;

  Clock clock_1 (.out(clock_1_out));
  nor nor_1 (Q, R, nQ);
  nor nor_2 (nQ, Q, S);
  S_R_Flip_Flop s_r_ff_1 (
    .S(RS_Flip_flop), .R(in_5), .clk(clock_1_out), .Q(out_13), .Qn(out_14));  // open: reset, preset
  Clock clock_2 (.out(clock_2_out));
  Clock clock_3 (.out(clock_3_out));
  not not_1 (not_1_out, D);
  not not_2 (not_2_out, D_2);
  and and_1 (and_1_out, clock_2_out, not_1_out);
  and and_2 (and_2_out, clock_2_out, D);
  not not_3 (not_3_out, clock_3_out);
  and and_3 (and_3_out, clock_3_out, not_2_out);
  and and_4 (and_4_out, clock_3_out, D_2);
  D_Flip_Flop d_ff_1 (.D(in_7), .clk(clock_4_out), .Q(out_16), .Qn(out_18));  // open: preset, reset
  Clock clock_4 (.out(clock_4_out));
  nor nor_3 (Q_2, and_1_out, nQ_2);
  nor nor_4 (nQ_2, Q_2, and_2_out);
  nor nor_5 (nor_5_out, and_3_out, nor_6_out);
  nor nor_6 (nor_6_out, nor_5_out, and_4_out);
  not not_4 (not_4_out, nor_5_out);
  D_Flip_Flop d_ff_2 (.D(d_ff_2_qn), .clk(clock_5_out), .Q(out_17), .Qn(d_ff_2_qn));  // open: preset, reset
  Clock clock_5 (.out(clock_5_out));
  and and_5 (and_5_out, not_3_out, not_4_out);
  and and_6 (and_6_out, not_3_out, nor_5_out);
  nor nor_7 (Q_3, and_5_out, nQ_3);
  nor nor_8 (nQ_3, Q_3, and_6_out);

  // Notes on the sheet:
  //   RS Latch
  //   S=1 -> set output to 1
  //   S, R=0 -> hold values
  //   S, R=1 -> invalid
  //   R=1 -> reset output to 0
  //   D Latch
  //   C
  //   D Flip flop
  //   C
  //   C=1
  //   C, D=1 ->set output to 1
  //   C=1, D=0 -> reset output to 0
  //   C=0 ->hold values
  //   S, R=1 -> impossible
  //   - write D into 1st latch
  //   - Q does not change
  //   R
  //   S
  //   R
  //   S
  //   D flip-flop
  //   C=0
  //   Q
  //   !Q
  //   - stop writing D
  //   C
  //   D
  //   - value from 1st latch written to second latch & read out
  //   R
  //   Toggle
  //   S
endmodule
