// Logisim project OverFlowDetectionCorrectedCircuit.circ as structural Verilog: 1 circuit, main circuit main
module main (
  input  SignBitA,
  input  SignBitB,
  input  ResultSignBit,
  input  CarryOut,
  input  AddSubCMD,
  output Overflow,
  output CarryFlagInOtherArchitectures
);

  wire and_1_out, not_1_out, xor_1_out, xor_2_out;

  xor xor_1 (xor_1_out, SignBitA, SignBitB);
  not not_1 (not_1_out, xor_1_out);
  xor xor_2 (xor_2_out, SignBitB, ResultSignBit);
  xor xor_3 (CarryFlagInOtherArchitectures, CarryOut, AddSubCMD);
  and and_1 (and_1_out, not_1_out, xor_2_out);
  or or_1 (Overflow, and_1_out, CarryFlagInOtherArchitectures);

  // Notes on the sheet:
  //   Result Sign Differs from Input Sign Check
  //   UnSignedOverFlowCheck
  //   Similar Sign Check
  //   If Both Conditions are true (I.e., inputs have similar sign and the result sign differes, then Sign overflow happens)
endmodule
