// Logisim project SequentialDivider v1.1.circ as structural Verilog: 6 circuits, main circuit Divider
module Divider (
  input  RESET,
  input  [3:0] Dividend,
  input  [3:0] Divisor,
  output [3:0] Quotient,
  output [3:0] Remainder,
  output DONE
);

  wire clock_1_out;
  wire [7:0] divisor_register_1_d0;

  Clock clock_1 (.out(clock_1_out));
  Divisor_register divisor_register_1 (
    .divisor(Divisor), .clk(clock_1_out), .D7(divisor_register_1_d0[7]), .D6(divisor_register_1_d0[6]),
    .D5(divisor_register_1_d0[5]), .D4(divisor_register_1_d0[4]), .D3(divisor_register_1_d0[3]),
    .D2(divisor_register_1_d0[2]), .D1(divisor_register_1_d0[1]), .D0(divisor_register_1_d0[0]));
  Counter #(.max('h0), .width(1)) counter_1 ();  // open: clr, load, up, count, clk, D, carry, Q

  // Notes on the sheet:
  //   First name LAST NAME, Student Number
endmodule

module Divisor_register (
  input  [3:0] divisor,
  input  clk,
  output D7,
  output D6,
  output D5,
  output D4,
  output D3,
  output D2,
  output D1,
  output D0
);

  D_Flip_Flop d_ff_1 (.D(divisor[3]), .clk(clk), .Q(D7));  // open: Qn, preset, reset
  D_Flip_Flop d_ff_2 (.D(divisor[2]), .clk(clk), .Q(D6));  // open: Qn, preset, reset
  D_Flip_Flop d_ff_3 (.D(divisor[1]), .clk(clk), .Q(D5));  // open: Qn, preset, reset
  D_Flip_Flop d_ff_4 (.D(divisor[0]), .clk(clk), .Q(D4));  // open: Qn, preset, reset
  D_Flip_Flop d_ff_5 (.D(1'b0), .clk(clk), .Q(D3));  // open: Qn, preset, reset
  D_Flip_Flop d_ff_6 (.D(1'b0), .clk(clk), .Q(D2));  // open: Qn, preset, reset
  D_Flip_Flop d_ff_7 (.D(1'b0), .clk(clk), .Q(D1));  // open: Qn, preset, reset
  D_Flip_Flop d_ff_8 (.D(1'b0), .clk(clk), .Q(D0));  // open: Qn, preset, reset
endmodule

module shift_right_register (
  input  in_1,
  input  clk,
  output D7,
  output D6,
  output D5,
  output D4,
  output D3,
  output D2,
  output D1,
  output D0
);

  D_Flip_Flop d_ff_1 (.D(in_1), .clk(clk), .Q(D7));  // open: Qn, preset, reset
  Register register_1 ();  // open: D, en, clk, Q, clr
  D_Flip_Flop d_ff_2 (.D(D7), .clk(clk), .Q(D6));  // open: Qn, preset, reset
  D_Flip_Flop d_ff_3 (.D(D6), .clk(clk), .Q(D5));  // open: Qn, preset, reset
  // Shift_Register shift_register_1: pin names not known
  D_Flip_Flop d_ff_4 (.D(D5), .clk(clk), .Q(D4));  // open: Qn, preset, reset
  D_Flip_Flop d_ff_5 (.D(D4), .clk(clk), .Q(D3));  // open: Qn, preset, reset
  D_Flip_Flop d_ff_6 (.D(D3), .clk(clk), .Q(D2));  // open: Qn, preset, reset
  D_Flip_Flop d_ff_7 (.D(D2), .clk(clk), .Q(D1));  // open: Qn, preset, reset
  D_Flip_Flop d_ff_8 (.D(D1), .clk(clk), .Q(D0));  // open: Qn, preset, reset
endmodule

module ALU (
  input  [7:0] remainder,
  input  [7:0] divisor,
  input  shift,
  input  clk,
  input  [3:0] quotient,
  output [7:0] remainder_after,
  output [3:0] Q_output
);

  wire not_1_out, not_2_out, subtractor_1_bout;
  wire [7:0] subtractor_1_out;

  not not_1 (not_1_out, subtractor_1_bout);
  not not_2 (not_2_out, shift);
  // Shift_Register #(.length(4)) shift_register_1: pin names not known; wires that end beside it: 1'b0, not_2_out, shift, clk, not_1_out, quotient[0], quotient[1], quotient[2], quotient[3], Q_output[0], Q_output[1], Q_output[2], Q_output[3]
  Subtractor subtractor_1 (.a(remainder), .b(divisor), .out(subtractor_1_out), .bout(subtractor_1_bout));  // open: bin
  Multiplexer #(.width(8)) multiplexer_1 (
    .in0(subtractor_1_out), .in1(remainder), .out(remainder_after), .sel(subtractor_1_bout));

  // Notes on the sheet:
  //   1=negative, restore remainder
  //   0=positive, R = R-D
  //   0=positive, REM>0,shift left quotient, Q0=1
  //   1 =negative, REM <0, shift left quotient, Q0=0
endmodule

module Divisor_right_shifter (
  input  clk,
  input  R,
  input  shift,
  input  [7:0] divisor,
  output [7:0] divisor_shifted
);

  wire not_1_out;

  not not_1 (not_1_out, shift);
  // Shift_Register shift_register_1: pin names not known; wires that end beside it: R, not_1_out, clk, 1'b0, divisor[7], divisor[6], divisor[5], divisor[4], divisor[3], divisor[2], divisor[1], divisor[0], shift, divisor_shifted[7], divisor_shifted[6], divisor_shifted[5], divisor_shifted[4], divisor_shifted[3], divisor_shifted[2], divisor_shifted[1], divisor_shifted[0]
endmodule

module one_step (
  input  [7:0] remainder,
  input  [7:0] divisor,
  input  clk,
  input  [3:0] quotient
);

  wire undriven;

  ALU alu_1 (
    .remainder(remainder), .divisor(divisor), .shift(undriven), .clk(clk), .quotient(quotient));  // open: remainder_after, Q_output
endmodule
