// Logisim project SevenSegDec.circ as structural Verilog: 1 circuit, main circuit SevenSegDec
module SevenSegDec (
  input  A3,
  input  A2,
  input  A1,
  input  A0,
  output S0,
  output S1,
  output S2,
  output S3,
  output S4,
  output S5,
  output S6
);

  wire and_1_out, and_2_out, and_3_out, and_4_out, not_1_out, not_2_out, not_3_out, not_4_out, not_5_out,
       not_6_out, not_7_out, not_8_out, not_9_out, not_10_out, not_11_out, not_12_out, not_13_out, or_1_out,
       or_5_out;

  not not_1 (not_1_out, A1);
  or or_1 (or_1_out, A3, A2, A1, A0);
  or or_2 (S3, A3, A2, A1, A0);
  or or_3 (S2, A3, A2, A1);
  or or_4 (S0, A3, A2, not_1_out, A0);
  not not_2 (not_2_out, A2);
  not not_3 (not_3_out, A0);
  not not_4 (not_4_out, A3);
  not not_5 (not_5_out, A2);
  not not_6 (not_6_out, A1);
  not not_7 (not_7_out, A0);
  not not_8 (not_8_out, A3);
  not not_9 (not_9_out, A2);
  not not_10 (not_10_out, A0);
  not not_11 (not_11_out, A3);
  not not_12 (not_12_out, A2);
  or or_5 (or_5_out, A3, not_2_out, A1, not_3_out);
  and and_1 (and_1_out, not_4_out, not_5_out, not_6_out, not_7_out);
  and and_2 (and_2_out, not_8_out, not_9_out, A1, not_10_out);
  and and_3 (and_3_out, not_11_out, not_12_out, A1, A0);
  not not_13 (not_13_out, A3);
  and and_4 (and_4_out, not_13_out, A2, A1, A0);
  and and_5 (S1, or_1_out, or_5_out);
  or or_6 (S4, and_1_out, and_2_out, and_3_out, and_4_out);
  _7_Segment_Display u_7_segment_display_1 (.g(S0), .f(S1), .a(S2), .b(S3), .e(S4), .d(S3), .c(S3));  // open: dp

  assign S5 = S3;
  assign S6 = S3;

  // Notes on the sheet:
  //   Rita Yang,260893989
endmodule
