// Logisim project flipflops.circ as structural Verilog: 1 circuit, main circuit main
module main (
  input  C,
  input  A,
  input  B,
  input  R,
  input  S,
  output sum,
  output carry,
  output Q,
  output internal_Q
);

  wire and_1_out, and_2_out, xor_1_out;

  xor xor_1 (xor_1_out, A, B);
  and and_1 (and_1_out, A, B);
  xor xor_2 (sum, xor_1_out, C);
  and and_2 (and_2_out, C, xor_1_out);
  nor nor_1 (Q, R, internal_Q);
  nor nor_2 (internal_Q, Q, S);
  or or_1 (carry, and_2_out, and_1_out);

  // Notes on the sheet:
  //   1-bit half adder 
  //   R-S flip flop
endmodule
